# Fritzing sketch WiFi_Device_Sketch (saved by Fritzing 1.0.1rc)

parts:
  M1 = Humidity and Temperature Sensor DHT11
  DHT1 = DHT22 Humidity and Temperature Sensor
  DS1 = DS18B20 1-Wire Temperature Sensor Probe
  IC1 = DIP - 6 pins [chip_label="5V RELAY" package="DIP (Dual Inline) [THT]"]
  IC4 = DIP - 6 pins [chip_label="5V RELAY" package="DIP (Dual Inline) [THT]"]
  IC3 = DIP - 6 pins [chip_label="5V RELAY" package="DIP (Dual Inline) [THT]"]
  IC2 = DIP - 6 pins [chip_label="5V RELAY" package="DIP (Dual Inline) [THT]"]
  R2 = Resistor [tolerance=±5% resistance=10k package="2010 [SMD]"]
  R3 = Resistor [tolerance=±5% resistance=10k package="2010 [SMD]"]
  U3 = TXS0108 [part_number=TXS0108EPW package=TSSOP]
  VCC1 = 4 x AAA Battery Mount
  C3 = Capacitor [package=1210]
  C4 = Capacitor [package=1210]
  Z1 = VARISTOR [package=0603-res]
  A1 = nRF7002-DK
  J1 = Basic Servo

nets:
  N1: M1.Vcc, R2.Pin_0
  N2: M1.Data, R2.Pin_1, A1.Pin_54, A1.Pin_60
  GND: M1.GND, DHT1.GND, DS1.GND, IC1.DC-, IC4.DC-, IC3.DC-, IC2.DC-, U3.GND, VCC1.-, C3.2, C4.2, Z1.1, A1.Pin_19, A1.Pin_103, A1.Pin_123, A1.Pin_155, A1.Pin_173, A1.Pin_210, J1.gnd
  VDD: DHT1.VDD, DS1.VDD, IC1.DC+, IC4.DC+, IC3.DC+, IC2.DC+, R3.Pin_0, VCC1.+
  N3: DHT1.DATA, R3.Pin_1, A1.Pin_53, A1.Pin_59
  N4: DS1.DQ, A1.Pin_51, A1.Pin_52, A1.Pin_137
  N5: IC1.IN, U3.B7
  N6: IC4.IN, U3.B4
  N7: IC3.IN, U3.B5
  N8: IC2.IN, U3.B6
  N9: U3.VccA, C3.1
  N10: U3.A4, A1.Pin_185
  N11: U3.A5, A1.Pin_184
  N12: U3.A6, A1.Pin_183
  N13: U3.A7, A1.Pin_182
  N14: U3.OE, Z1.2, A1.Pin_186
  N15: U3.VccB, C4.1, J1.vcc
  N16: A1.Pin_188, J1.pulse

custom parts:
  Humidity and Temperature Sensor DHT11: Digital relative humidity & temperature sensor DHT11
  DIP - 6 pins: A DIP stand-in part for whatever IC you want. With 6 pins on a 300mil dual inline package (DIP) footprint.
  TXS0108: This 8-bit non-inverting translator uses two separate configurable power-supply rails. The A port tracks the VCCA pin supply voltage. The VCCA pin accepts any supply voltage between 1.2 V and 3.6 V. The B port tracks the VCCB pin supply voltage. The VCCB pin accepts any supply voltage between 1.65 V and 5.5 V. Two input supply pins allows for low Voltage bidirectional translation between any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
  nRF7002-DK: The nRF7002 DK is the development kit for the nRF7002, and nRF7001 Wi-Fi 6 Companion ICs.
